// Logisim project counter.circ as structural Verilog: 1 circuit, main circuit counter
module counter (
  input  increment,
  input  zero,
  output [3:0] out_3,
  output [3:0] out_4,
  output [3:0] out_5
);

  wire comparator_1_eq, comparator_2_eq, comparator_3_eq, or_1_out, or_2_out, or_3_out;

  Pull_Resistor pull_resistor_1 (.node(increment));
  Pull_Resistor pull_resistor_2 (.node(zero));
  Counter #(.width(4), .max('hf)) counter_1 (
    .count(1'b1), .Q(out_5), .clk(increment), .clr(or_1_out));  // open: load, D, carry
  or or_1 (or_1_out, zero, comparator_1_eq);
  Comparator #(.width(4)) comparator_1 (.a(out_5), .b(4'b1010), .eq(comparator_1_eq));  // open: gt, lt
  Counter #(.width(4), .max('hf)) counter_2 (
    .count(1'b1), .Q(out_4), .clk(comparator_1_eq), .clr(or_2_out));  // open: load, D, carry
  or or_2 (or_2_out, zero, comparator_2_eq);
  Comparator #(.width(4)) comparator_2 (.a(out_4), .b(4'b1010), .eq(comparator_2_eq));  // open: gt, lt
  Counter #(.width(4), .max('hf)) counter_3 (
    .count(1'b1), .Q(out_3), .clk(comparator_2_eq), .clr(or_3_out));  // open: load, D, carry
  or or_3 (or_3_out, zero, comparator_3_eq);
  Comparator #(.width(4)) comparator_3 (.a(out_3), .b(4'b1010), .eq(comparator_3_eq));  // open: gt, lt

  // Other names for the same wires on the sheet: digit1[3:0] = out_5; digit2[3:0] = out_4; digit3[3:0] = out_3
endmodule
