// Logisim project display-controller.circ as structural Verilog: 2 circuits, main circuit display_controller
module display_controller (
  input  [3:0] X_coord,
  input  [3:0] Y_coord,
  input  pixel_state,
  input  write,
  input  pixel_check,
  input  game_over,
  output [15:0] c00,
  output [15:0] c01,
  output [15:0] c02,
  output [15:0] c03,
  output [15:0] c04,
  output checked,
  output [15:0] c05,
  output [15:0] c06,
  output [15:0] c07,
  output [15:0] c08,
  output [15:0] c09,
  output [15:0] c10,
  output [15:0] c11,
  output [15:0] c12,
  output [15:0] c13,
  output [15:0] c14,
  output [15:0] c15
);

  wire and_17_out, and_18_out, and_19_out, and_20_out, and_21_out, and_22_out, and_23_out, and_24_out,
       and_25_out, and_26_out, and_27_out, and_28_out, and_29_out, and_30_out, and_31_out, and_32_out,
       and_33_out, and_34_out, and_35_out, and_36_out, and_37_out, and_38_out, and_39_out, and_40_out,
       and_41_out, and_42_out, and_43_out, and_44_out, and_45_out, and_46_out, and_47_out, and_48_out,
       not_2_out, not_3_out, not_4_out, not_5_out, not_6_out, not_7_out, not_8_out, not_9_out, not_10_out,
       not_11_out, not_12_out, not_13_out, not_14_out, not_15_out, not_16_out, not_17_out, or_1_out,
       or_2_out, or_3_out, or_4_out, wrt0, wrt1, wrt2, wrt3, wrt4, wrt5, wrt6, wrt7, wrt8, wrt9, wrt10,
       wrt11, wrt12, wrt13, wrt14, wrt15;
  wire [15:0] and_1_out, and_2_out, and_3_out, and_4_out, and_5_out, and_6_out, and_7_out, and_8_out,
       and_9_out, and_10_out, and_11_out, and_12_out, and_13_out, and_14_out, and_15_out, and_16_out,
       and_49_out, and_50_out, and_51_out, and_52_out, and_53_out, and_54_out, and_55_out, and_56_out,
       and_57_out, and_58_out, and_59_out, and_60_out, and_61_out, and_62_out, and_63_out, and_64_out,
       checked_value, demultiplexer_3_out0, end00, end01, end02, end03, end04, end05, end06, end07, end08,
       end09, end10, end11, end12, end13, end14, end15, mask, or_6_out, or_7_out, or_8_out, or_9_out,
       or_10_out, or_11_out, or_12_out, or_13_out, or_14_out, or_15_out, or_16_out, or_17_out, or_18_out,
       or_19_out, or_20_out, or_21_out, register_1_q, register_2_q, register_3_q, register_4_q, register_5_q,
       register_6_q, register_7_q, register_8_q, register_9_q, register_10_q, register_11_q, register_12_q,
       register_13_q, register_14_q, register_15_q, register_16_q, value;

  Pull_Resistor pull_resistor_1 (.node(pixel_check));
  or or_1 (or_1_out, pixel_check, write);
  Demultiplexer #(.select(4)) demultiplexer_1 (
    .out0(wrt0), .out1(wrt1), .out2(wrt2), .out3(wrt3), .out4(wrt4), .out5(wrt5), .out6(wrt6), .out7(wrt7),
    .out8(wrt8), .out9(wrt9), .out10(wrt10), .out11(wrt11), .out12(wrt12), .out13(wrt13), .out14(wrt14),
    .out15(wrt15), .in(or_1_out), .sel(X_coord));  // open: en
  or or_2 (or_2_out, pixel_state, pixel_check);
  Demultiplexer #(.select(4)) demultiplexer_2 (
    .out0(value[0]), .out1(value[1]), .out2(value[2]), .out3(value[3]), .out4(value[4]), .out5(value[5]),
    .out6(value[6]), .out7(value[7]), .out8(value[8]), .out9(value[9]), .out10(value[10]), .out11(value[11]),
    .out12(value[12]), .out13(value[13]), .out14(value[14]), .out15(value[15]), .in(or_2_out), .sel(Y_coord));  // open: en
  Demultiplexer #(.select(4)) demultiplexer_3 (
    .out0(demultiplexer_3_out0[0]), .out1(demultiplexer_3_out0[1]), .out2(demultiplexer_3_out0[2]),
    .out3(demultiplexer_3_out0[3]), .out4(demultiplexer_3_out0[4]), .out5(demultiplexer_3_out0[5]),
    .out6(demultiplexer_3_out0[6]), .out7(demultiplexer_3_out0[7]), .out8(demultiplexer_3_out0[8]),
    .out9(demultiplexer_3_out0[9]), .out10(demultiplexer_3_out0[10]), .out11(demultiplexer_3_out0[11]),
    .out12(demultiplexer_3_out0[12]), .out13(demultiplexer_3_out0[13]), .out14(demultiplexer_3_out0[14]),
    .out15(demultiplexer_3_out0[15]), .in(1'b1), .sel(Y_coord));  // open: en
  or or_3 (or_3_out, checked_value[0], checked_value[1], checked_value[2], checked_value[3], checked_value[4], checked_value[5], checked_value[6]);
  or or_4 (or_4_out, checked_value[7], checked_value[8], checked_value[9], checked_value[10], checked_value[11], checked_value[12], checked_value[13]);
  // Probe on 8'h1c
  // Probe on 8'h22
  // Probe on 8'h22
  // Probe on 8'h1c
  // Probe on {8{1'b0}}
  // Probe on 8'h1e
  // Probe on 8'h20
  // Probe on 8'h1e
  // Probe on {8{1'b0}}
  // Probe on 8'h3e
  // Probe on 8'h2a
  // Probe on {8{1'b0}}
  // Probe on 8'h3e
  // Probe on 8'ha
  // Probe on 8'ha
  // Probe on 8'h34
  or or_5 (checked, or_3_out, or_4_out, checked_value[14], checked_value[15]);
  // Probe on 8'h38
  // Probe on 8'h44
  // Probe on 8'h64
  // Probe on {8{1'b0}}
  // Probe on 8'h78
  // Probe on 8'h24
  // Probe on 8'h78
  // Probe on {8{1'b0}}
  // Probe on 8'h7c
  // Probe on 8'h8
  // Probe on 8'h10
  // Probe on 8'h8
  // Probe on 8'h7c
  // Probe on {8{1'b0}}
  // Probe on 8'h7c
  // Probe on 8'h54
  // Probe on value
  // Probe on mask
  assign mask = ~demultiplexer_3_out0;  // NOT_Gate not_1, 16 bits wide
  reverser reverser_1 (.in(16'h1c38), .reversed(end00));
  reverser reverser_2 (.in(16'h2244), .reversed(end01));
  reverser reverser_3 (.in(16'h2264), .reversed(end02));
  reverser reverser_4 (.in(16'h1c00), .reversed(end03));
  reverser reverser_5 (.in(16'h78), .reversed(end04));
  reverser reverser_6 (.in(16'h1e24), .reversed(end05));
  reverser reverser_7 (.in(16'h2078), .reversed(end06));
  reverser reverser_8 (.in(16'h1e00), .reversed(end07));
  reverser reverser_9 (.in(16'h7c), .reversed(end08));
  reverser reverser_10 (.in(16'h3e08), .reversed(end09));
  reverser reverser_11 (.in(16'h2a10), .reversed(end10));
  reverser reverser_12 (.in(16'h8), .reversed(end11));
  reverser reverser_13 (.in(16'h3e7c), .reversed(end12));
  reverser reverser_14 (.in(16'ha00), .reversed(end13));
  reverser reverser_15 (.in(16'ha7c), .reversed(end14));
  reverser reverser_16 (.in(16'h3454), .reversed(end15));
  assign and_1_out = register_1_q & mask;  // AND_Gate and_1, 16 bits wide
  assign and_2_out = register_2_q & mask;  // AND_Gate and_2, 16 bits wide
  assign and_3_out = register_3_q & mask;  // AND_Gate and_3, 16 bits wide
  assign and_4_out = register_4_q & mask;  // AND_Gate and_4, 16 bits wide
  assign and_5_out = register_5_q & mask;  // AND_Gate and_5, 16 bits wide
  assign and_6_out = register_6_q & mask;  // AND_Gate and_6, 16 bits wide
  assign and_7_out = register_7_q & mask;  // AND_Gate and_7, 16 bits wide
  assign and_8_out = register_8_q & mask;  // AND_Gate and_8, 16 bits wide
  assign and_9_out = register_9_q & mask;  // AND_Gate and_9, 16 bits wide
  assign and_10_out = register_10_q & mask;  // AND_Gate and_10, 16 bits wide
  assign and_11_out = register_11_q & mask;  // AND_Gate and_11, 16 bits wide
  assign and_12_out = register_12_q & mask;  // AND_Gate and_12, 16 bits wide
  assign and_13_out = register_13_q & mask;  // AND_Gate and_13, 16 bits wide
  assign and_14_out = register_14_q & mask;  // AND_Gate and_14, 16 bits wide
  assign and_15_out = register_15_q & mask;  // AND_Gate and_15, 16 bits wide
  assign and_16_out = register_16_q & mask;  // AND_Gate and_16, 16 bits wide
  assign or_6_out = value | and_1_out;  // OR_Gate or_6, 16 bits wide
  Register #(.width(16)) register_1 (.D(or_6_out), .Q(register_1_q), .clk(and_17_out));  // open: en, clr
  and and_17 (and_17_out, write, wrt0);
  assign or_7_out = value | and_2_out;  // OR_Gate or_7, 16 bits wide
  Register #(.width(16)) register_2 (.D(or_7_out), .Q(register_2_q), .clk(and_18_out));  // open: en, clr
  and and_18 (and_18_out, write, wrt1);
  Register #(.width(16)) register_3 (.D(or_8_out), .Q(register_3_q), .clk(and_19_out));  // open: en, clr
  assign or_8_out = value | and_3_out;  // OR_Gate or_8, 16 bits wide
  and and_19 (and_19_out, write, wrt2);
  assign or_9_out = value | and_4_out;  // OR_Gate or_9, 16 bits wide
  Register #(.width(16)) register_4 (.D(or_9_out), .Q(register_4_q), .clk(and_20_out));  // open: en, clr
  and and_20 (and_20_out, write, wrt3);
  assign or_10_out = value | and_5_out;  // OR_Gate or_10, 16 bits wide
  Register #(.width(16)) register_5 (.D(or_10_out), .Q(register_5_q), .clk(and_21_out));  // open: en, clr
  and and_21 (and_21_out, write, wrt4);
  Register #(.width(16)) register_6 (.D(or_11_out), .Q(register_6_q), .clk(and_22_out));  // open: en, clr
  assign or_11_out = value | and_6_out;  // OR_Gate or_11, 16 bits wide
  and and_22 (and_22_out, write, wrt5);
  Register #(.width(16)) register_7 (.D(or_12_out), .Q(register_7_q), .clk(and_23_out));  // open: en, clr
  assign or_12_out = value | and_7_out;  // OR_Gate or_12, 16 bits wide
  and and_23 (and_23_out, write, wrt6);
  Register #(.width(16)) register_8 (.D(or_13_out), .Q(register_8_q), .clk(and_24_out));  // open: en, clr
  assign or_13_out = value | and_8_out;  // OR_Gate or_13, 16 bits wide
  and and_24 (and_24_out, write, wrt7);
  Register #(.width(16)) register_9 (.D(or_14_out), .Q(register_9_q), .clk(and_25_out));  // open: en, clr
  assign or_14_out = value | and_9_out;  // OR_Gate or_14, 16 bits wide
  and and_25 (and_25_out, write, wrt8);
  Register #(.width(16)) register_10 (.D(or_15_out), .Q(register_10_q), .clk(and_26_out));  // open: en, clr
  assign or_15_out = value | and_10_out;  // OR_Gate or_15, 16 bits wide
  and and_26 (and_26_out, write, wrt9);
  Register #(.width(16)) register_11 (.D(or_16_out), .Q(register_11_q), .clk(and_27_out));  // open: en, clr
  assign or_16_out = value | and_11_out;  // OR_Gate or_16, 16 bits wide
  and and_27 (and_27_out, write, wrt10);
  assign or_17_out = value | and_12_out;  // OR_Gate or_17, 16 bits wide
  Register #(.width(16)) register_12 (.D(or_17_out), .Q(register_12_q), .clk(and_28_out));  // open: en, clr
  and and_28 (and_28_out, write, wrt11);
  assign or_18_out = value | and_13_out;  // OR_Gate or_18, 16 bits wide
  Register #(.width(16)) register_13 (.D(or_18_out), .Q(register_13_q), .clk(and_29_out));  // open: en, clr
  and and_29 (and_29_out, write, wrt12);
  Register #(.width(16)) register_14 (.D(or_19_out), .Q(register_14_q), .clk(and_30_out));  // open: en, clr
  assign or_19_out = value | and_14_out;  // OR_Gate or_19, 16 bits wide
  and and_30 (and_30_out, write, wrt13);
  Register #(.width(16)) register_15 (.D(or_20_out), .Q(register_15_q), .clk(and_31_out));  // open: en, clr
  assign or_20_out = value | and_15_out;  // OR_Gate or_20, 16 bits wide
  and and_31 (and_31_out, write, wrt14);
  Register #(.width(16)) register_16 (.D(or_21_out), .Q(register_16_q), .clk(and_32_out));  // open: en, clr
  assign or_21_out = value | and_16_out;  // OR_Gate or_21, 16 bits wide
  and and_32 (and_32_out, write, wrt15);
  not not_2 (not_2_out, game_over);
  and and_33 (and_33_out, pixel_check, wrt0);
  not not_3 (not_3_out, game_over);
  and and_34 (and_34_out, pixel_check, wrt1);
  not not_4 (not_4_out, game_over);
  and and_35 (and_35_out, pixel_check, wrt2);
  not not_5 (not_5_out, game_over);
  and and_36 (and_36_out, pixel_check, wrt3);
  not not_6 (not_6_out, game_over);
  and and_37 (and_37_out, pixel_check, wrt4);
  not not_7 (not_7_out, game_over);
  and and_38 (and_38_out, pixel_check, wrt5);
  not not_8 (not_8_out, game_over);
  and and_39 (and_39_out, pixel_check, wrt6);
  not not_9 (not_9_out, game_over);
  and and_40 (and_40_out, pixel_check, wrt7);
  not not_10 (not_10_out, game_over);
  and and_41 (and_41_out, pixel_check, wrt8);
  not not_11 (not_11_out, game_over);
  and and_42 (and_42_out, pixel_check, wrt9);
  not not_12 (not_12_out, game_over);
  and and_43 (and_43_out, pixel_check, wrt10);
  not not_13 (not_13_out, game_over);
  and and_44 (and_44_out, pixel_check, wrt11);
  not not_14 (not_14_out, game_over);
  and and_45 (and_45_out, pixel_check, wrt12);
  not not_15 (not_15_out, game_over);
  and and_46 (and_46_out, pixel_check, wrt13);
  not not_16 (not_16_out, game_over);
  and and_47 (and_47_out, pixel_check, wrt14);
  not not_17 (not_17_out, game_over);
  and and_48 (and_48_out, pixel_check, wrt15);
  assign c00 = not_2_out ? register_1_q : 16'bz;  // Controlled_Buffer controlled_buffer_1
  assign c00 = game_over ? end00 : 16'bz;  // Controlled_Buffer controlled_buffer_2
  assign and_49_out = register_1_q & value;  // AND_Gate and_49, 16 bits wide
  assign checked_value = and_33_out ? and_49_out : 16'bz;  // Controlled_Buffer controlled_buffer_3
  assign c01 = not_3_out ? register_2_q : 16'bz;  // Controlled_Buffer controlled_buffer_4
  assign c01 = game_over ? end01 : 16'bz;  // Controlled_Buffer controlled_buffer_5
  assign and_50_out = register_2_q & value;  // AND_Gate and_50, 16 bits wide
  assign checked_value = and_34_out ? and_50_out : 16'bz;  // Controlled_Buffer controlled_buffer_6
  assign c02 = game_over ? end02 : 16'bz;  // Controlled_Buffer controlled_buffer_7
  assign c02 = not_4_out ? register_3_q : 16'bz;  // Controlled_Buffer controlled_buffer_8
  assign checked_value = and_35_out ? and_51_out : 16'bz;  // Controlled_Buffer controlled_buffer_9
  assign and_51_out = register_3_q & value;  // AND_Gate and_51, 16 bits wide
  assign c03 = game_over ? end03 : 16'bz;  // Controlled_Buffer controlled_buffer_10
  assign c03 = not_5_out ? register_4_q : 16'bz;  // Controlled_Buffer controlled_buffer_11
  assign checked_value = and_36_out ? and_52_out : 16'bz;  // Controlled_Buffer controlled_buffer_12
  assign and_52_out = register_4_q & value;  // AND_Gate and_52, 16 bits wide
  assign c04 = game_over ? end04 : 16'bz;  // Controlled_Buffer controlled_buffer_13
  assign c04 = not_6_out ? register_5_q : 16'bz;  // Controlled_Buffer controlled_buffer_14
  assign checked_value = and_37_out ? and_53_out : 16'bz;  // Controlled_Buffer controlled_buffer_15
  assign and_53_out = register_5_q & value;  // AND_Gate and_53, 16 bits wide
  assign c05 = not_7_out ? register_6_q : 16'bz;  // Controlled_Buffer controlled_buffer_16
  assign c05 = game_over ? end05 : 16'bz;  // Controlled_Buffer controlled_buffer_17
  assign checked_value = and_38_out ? and_54_out : 16'bz;  // Controlled_Buffer controlled_buffer_18
  assign and_54_out = register_6_q & value;  // AND_Gate and_54, 16 bits wide
  assign c06 = game_over ? end06 : 16'bz;  // Controlled_Buffer controlled_buffer_19
  assign c06 = not_8_out ? register_7_q : 16'bz;  // Controlled_Buffer controlled_buffer_20
  assign checked_value = and_39_out ? and_55_out : 16'bz;  // Controlled_Buffer controlled_buffer_21
  assign and_55_out = register_7_q & value;  // AND_Gate and_55, 16 bits wide
  assign c07 = game_over ? end07 : 16'bz;  // Controlled_Buffer controlled_buffer_22
  assign c07 = not_9_out ? register_8_q : 16'bz;  // Controlled_Buffer controlled_buffer_23
  assign and_56_out = register_8_q & value;  // AND_Gate and_56, 16 bits wide
  assign checked_value = and_40_out ? and_56_out : 16'bz;  // Controlled_Buffer controlled_buffer_24
  assign c08 = not_10_out ? register_9_q : 16'bz;  // Controlled_Buffer controlled_buffer_25
  assign c08 = game_over ? end08 : 16'bz;  // Controlled_Buffer controlled_buffer_26
  assign and_57_out = register_9_q & value;  // AND_Gate and_57, 16 bits wide
  assign checked_value = and_41_out ? and_57_out : 16'bz;  // Controlled_Buffer controlled_buffer_27
  assign c09 = not_11_out ? register_10_q : 16'bz;  // Controlled_Buffer controlled_buffer_28
  assign c09 = game_over ? end09 : 16'bz;  // Controlled_Buffer controlled_buffer_29
  assign and_58_out = register_10_q & value;  // AND_Gate and_58, 16 bits wide
  assign checked_value = and_42_out ? and_58_out : 16'bz;  // Controlled_Buffer controlled_buffer_30
  assign c10 = not_12_out ? register_11_q : 16'bz;  // Controlled_Buffer controlled_buffer_31
  assign c10 = game_over ? end10 : 16'bz;  // Controlled_Buffer controlled_buffer_32
  assign and_59_out = register_11_q & value;  // AND_Gate and_59, 16 bits wide
  assign checked_value = and_43_out ? and_59_out : 16'bz;  // Controlled_Buffer controlled_buffer_33
  assign c11 = game_over ? end11 : 16'bz;  // Controlled_Buffer controlled_buffer_34
  assign c11 = not_13_out ? register_12_q : 16'bz;  // Controlled_Buffer controlled_buffer_35
  assign and_60_out = register_12_q & value;  // AND_Gate and_60, 16 bits wide
  assign checked_value = and_44_out ? and_60_out : 16'bz;  // Controlled_Buffer controlled_buffer_36
  assign c12 = game_over ? end12 : 16'bz;  // Controlled_Buffer controlled_buffer_37
  assign c12 = not_14_out ? register_13_q : 16'bz;  // Controlled_Buffer controlled_buffer_38
  assign and_61_out = register_13_q & value;  // AND_Gate and_61, 16 bits wide
  assign checked_value = and_45_out ? and_61_out : 16'bz;  // Controlled_Buffer controlled_buffer_39
  assign c13 = not_15_out ? register_14_q : 16'bz;  // Controlled_Buffer controlled_buffer_40
  assign c13 = game_over ? end13 : 16'bz;  // Controlled_Buffer controlled_buffer_41
  assign checked_value = and_46_out ? and_62_out : 16'bz;  // Controlled_Buffer controlled_buffer_42
  assign and_62_out = register_14_q & value;  // AND_Gate and_62, 16 bits wide
  assign c14 = game_over ? end14 : 16'bz;  // Controlled_Buffer controlled_buffer_43
  assign c14 = not_16_out ? register_15_q : 16'bz;  // Controlled_Buffer controlled_buffer_44
  assign checked_value = and_47_out ? and_63_out : 16'bz;  // Controlled_Buffer controlled_buffer_45
  assign and_63_out = register_15_q & value;  // AND_Gate and_63, 16 bits wide
  assign c15 = game_over ? end15 : 16'bz;  // Controlled_Buffer controlled_buffer_46
  assign c15 = not_17_out ? register_16_q : 16'bz;  // Controlled_Buffer controlled_buffer_47
  assign and_64_out = register_16_q & value;  // AND_Gate and_64, 16 bits wide
  assign checked_value = and_48_out ? and_64_out : 16'bz;  // Controlled_Buffer controlled_buffer_48
  Pull_Resistor pull_resistor_2 (.node(checked_value));
  // Probe on checked_value
  Pull_Resistor pull_resistor_3 (.node(checked_value));
  // Probe on checked_value
  Pull_Resistor pull_resistor_4 (.node(checked_value));
  // Probe on checked_value
  Pull_Resistor pull_resistor_5 (.node(checked_value));
  // Probe on checked_value
  Pull_Resistor pull_resistor_6 (.node(checked_value));
  // Probe on checked_value
  Pull_Resistor pull_resistor_7 (.node(checked_value));
  // Probe on checked_value
  Pull_Resistor pull_resistor_8 (.node(checked_value));
  // Probe on checked_value
  Pull_Resistor pull_resistor_9 (.node(checked_value));
  // Probe on checked_value
  Pull_Resistor pull_resistor_10 (.node(checked_value));
  // Probe on checked_value
  Pull_Resistor pull_resistor_11 (.node(checked_value));
  // Probe on checked_value
  Pull_Resistor pull_resistor_12 (.node(checked_value));
  // Probe on checked_value
  Pull_Resistor pull_resistor_13 (.node(checked_value));
  // Probe on checked_value
  Pull_Resistor pull_resistor_14 (.node(checked_value));
  // Probe on checked_value
  Pull_Resistor pull_resistor_15 (.node(checked_value));
  // Probe on checked_value
  Pull_Resistor pull_resistor_16 (.node(checked_value));
  // Probe on checked_value
  Pull_Resistor pull_resistor_17 (.node(checked_value));
  // Probe on checked_value

  // Other names for the same wires on the sheet: check = pixel_check; end = game_over
endmodule

module reverser (
  input  [15:0] in,
  output [15:0] reversed
);


  assign reversed = {in[0], in[1], in[2], in[3], in[4], in[5], in[6], in[7], in[8], in[9], in[10], in[11], in[12], in[13], in[14], in[15]};
endmodule
