// Logisim project one_pixel_circ.circ as structural Verilog: 2 circuits, main circuit main
module main (
);

  wire cdm_16_1_p1, cdm_16_1_p2, cdm_16_1_p3, cdm_16_1_p6, cdm_16_1_p7, cdm_16_1_p8, cdm_16_1_p9,
       clock_2_out, not_1_out;
  wire [3:0] bit_extender_1_out;
  wire [15:0] cdm_16_1_p4, cdm_16_1_p5, cdm_16_1_p10, cdm_16_1_p11, controlled_buffer_1_out,
       demultiplexer_1_out9, demultiplexer_1_out10, demultiplexer_1_out11, demultiplexer_1_out12,
       demultiplexer_1_out13, demultiplexer_1_out14, demultiplexer_1_out15, pull_resistor_1_node,
       pull_resistor_2_node, pull_resistor_3_node, pull_resistor_4_node, pull_resistor_5_node,
       pull_resistor_6_node, pull_resistor_7_node, pull_resistor_8_node, pull_resistor_9_node;

  // Probe on cdm_16_1_p2
  // Probe on cdm_16_1_p1
  // CdM_16 cdm_16_1: pin names not known; wires that end beside it: cdm_16_1_p1, cdm_16_1_p2, cdm_16_1_p3, cdm_16_1_p4, cdm_16_1_p5, cdm_16_1_p6, cdm_16_1_p7, cdm_16_1_p8, cdm_16_1_p9, cdm_16_1_p10, cdm_16_1_p11
  Clock clock_1 (.out(cdm_16_1_p3));
  Bit_Extender #(.in_width(16), .out_width(4)) bit_extender_1 (.in(cdm_16_1_p4), .out(bit_extender_1_out));
  // Probe on cdm_16_1_p4
  // Probe on cdm_16_1_p5
  Button button ();  // open: out
  assign controlled_buffer_1_out = not_1_out ? cdm_16_1_p10 : 16'bz;  // Controlled_Buffer controlled_buffer_1
  not not_1 (not_1_out, cdm_16_1_p7);
  assign cdm_16_1_p11 = cdm_16_1_p7 ? controlled_buffer_1_out : 16'bz;  // Controlled_Buffer controlled_buffer_2
  Button button_2 ();  // open: out
  Button v ();  // open: out
  Button button_3 ();  // open: out
  DotMatrix #(.matrixcols(16), .matrixrows(16)) dotmatrix_1 (
    .col0(pull_resistor_1_node), .col1(pull_resistor_9_node), .col2(pull_resistor_5_node),
    .col3(pull_resistor_3_node), .col4(pull_resistor_7_node), .col5(pull_resistor_8_node),
    .col6(pull_resistor_4_node), .col7(pull_resistor_6_node), .col8(pull_resistor_2_node),
    .col9(demultiplexer_1_out9), .col10(demultiplexer_1_out10), .col11(demultiplexer_1_out11),
    .col12(demultiplexer_1_out12), .col13(demultiplexer_1_out13), .col14(demultiplexer_1_out14),
    .col15(demultiplexer_1_out15));
  Pull_Resistor pull_resistor_1 (.node(pull_resistor_1_node));
  Clock clock_2 (.out(clock_2_out));
  Pull_Resistor pull_resistor_2 (.node(pull_resistor_2_node));
  Pull_Resistor pull_resistor_3 (.node(pull_resistor_3_node));
  Pull_Resistor pull_resistor_4 (.node(pull_resistor_4_node));
  Pull_Resistor pull_resistor_5 (.node(pull_resistor_5_node));
  Pull_Resistor pull_resistor_6 (.node(pull_resistor_6_node));
  Pull_Resistor pull_resistor_7 (.node(pull_resistor_7_node));
  Pull_Resistor pull_resistor_8 (.node(pull_resistor_8_node));
  Pull_Resistor pull_resistor_9 (.node(pull_resistor_9_node));
  Demultiplexer #(.select(4), .width(16)) demultiplexer_1 (
    .out0(pull_resistor_1_node), .out1(pull_resistor_9_node), .out2(pull_resistor_5_node),
    .out3(pull_resistor_3_node), .out4(pull_resistor_7_node), .out5(pull_resistor_8_node),
    .out6(pull_resistor_4_node), .out7(pull_resistor_6_node), .out8(pull_resistor_2_node),
    .out9(demultiplexer_1_out9), .out10(demultiplexer_1_out10), .out11(demultiplexer_1_out11),
    .out12(demultiplexer_1_out12), .out13(demultiplexer_1_out13), .out14(demultiplexer_1_out14),
    .out15(demultiplexer_1_out15), .in(cdm_16_1_p5), .sel(bit_extender_1_out));  // open: en
  // RAM ram_1: pin names not known; wires that end beside it: cdm_16_1_p9, cdm_16_1_p8, cdm_16_1_p6, clock_2_out, cdm_16_1_p7, controlled_buffer_1_out
  Pull_Resistor pull_resistor_10 (.node(demultiplexer_1_out9));
  Pull_Resistor pull_resistor_11 (.node(demultiplexer_1_out10));
  Pull_Resistor pull_resistor_12 (.node(demultiplexer_1_out12));
  Pull_Resistor pull_resistor_13 (.node(demultiplexer_1_out13));
  Pull_Resistor pull_resistor_14 (.node(demultiplexer_1_out11));
  Pull_Resistor pull_resistor_15 (.node(demultiplexer_1_out15));
  Pull_Resistor pull_resistor_16 (.node(demultiplexer_1_out14));
  DotMatrix #(.matrixcols(16), .matrixrows(16), .persist(1), .dotshape("circle")) dotmatrix_2 ();  // open: col0, col1, col2, col3, col4, col5, col6, col7, col8, col9, col10, col11, col12, col13, col14, col15
endmodule

module display_controller (
  input  [4:0] X_coord,
  input  [4:0] Y_coord,
  input  pixel_state,
  input  write
);

  Multiplexer multiplexer_1 ();  // open: in0, in1, out, sel, en
  Register register_1 ();  // open: D, en, Q, clk, clr
endmodule
